# Fritzing sketch Genesis Synth (saved by Fritzing 0.9.3b)
breadboards: 1

parts:
  Part1 = Arduino Mega 2560 (Rev3)
  S1 = SWITCH-MOMENTARY-2 [package=tactile-pth]  # not connected
  S2 = SWITCH-MOMENTARY-2 [package=tactile-pth]  # not connected
  S3 = SWITCH-MOMENTARY-2 [package=tactile-pth]  # not connected
  S4 = SWITCH-MOMENTARY-2 [package=tactile-pth]  # not connected
  S5 = SWITCH-MOMENTARY-2 [package=tactile-pth]  # not connected
  SP1 = SPEAKER [package=pcb_mount_speaker]  # not connected
  R1 = TRIMPOT [package=3386u]  # not connected
  YM2612 = IC, DIP package, 24 pins [chip_label=YM2612]
  LM386 = LM386 [package=dip08]  # not connected

nets:
  N1: Part1.D22, YM2612.pin2
  N2: Part1.D23, YM2612.pin3
  N3: Part1.D24, YM2612.pin4
  N4: Part1.D25, YM2612.pin5
  N5: Part1.D26, YM2612.pin6
  N6: Part1.D27, YM2612.pin7
  N7: Part1.D28, YM2612.pin8
  N8: Part1.D29, YM2612.pin9
  N9: Part1.D32, YM2612.pin11
  N10: Part1.D33, YM2612.pin14
  N11: Part1.D34, YM2612.pin15
